# Fritzing sketch cablage-pro-micro (saved by Fritzing 1.0.1rc)

parts:
  Pro_Micro1 = Pro Micro
  U1 = RJ45 Jack [package=rj45-8]
  S1 = Round Pushbutton

nets:
  N1: Pro_Micro1.GND#4, S1.leg0
  N2: Pro_Micro1.D7, S1.leg1
  N3: Pro_Micro1.D16/MOSI, U1.4
  N4: Pro_Micro1.D14/MISO, U1.3
  N5: Pro_Micro1.D15/SCLK, U1.5
  N6: Pro_Micro1.VCC, U1.1
  N7: Pro_Micro1.GND#23, U1.2

custom parts:
  Pro Micro: The SparkFun Pro Micro is a complete USB-based microcontoller development system, in a very small footprint, capable of implementing many types of projects. All programming can be done via the USB port.
